# Fritzing sketch KeyPad (saved by Fritzing 0.9.2b)

parts:
  Part2 = Arduino Uno (Rev3) - ICSP
  Matrix_keypad1 = KEYPAD 4x4

nets:
  N1: Part2.D8, Matrix_keypad1.col3
  N2: Part2.D9_PWM, Matrix_keypad1.col4
  N3: Part2.D2, Matrix_keypad1.row1
  N4: Part2.D3_PWM, Matrix_keypad1.row2
  N5: Part2.D4, Matrix_keypad1.row3
  N6: Part2.D5_PWM, Matrix_keypad1.row4
  N7: Part2.D6_PWM, Matrix_keypad1.col1
  N8: Part2.D7, Matrix_keypad1.col2

custom parts:
  KEYPAD 4x4: Matrix keypad 16 buttons, 4 rows x 4 columns
